# Fritzing sketch Wiring (saved by Fritzing 0.8.7b)

parts:
  LCM1602_IIC1 = LCM1602 IIC [part_number="LCM1602 IIC" chip_label="LCM1602 IIC" package="DIP (Dual Inline) [THT]"]
  U1 = LCD-16X2 [package=lcd-16x2]
  M1 = DOIT Esp32 DevKit v1 (30 pins long, 11 pins width) [part_number=ESP32S-PIN30]
  JP1 = Header 4 [package=jst-4-pth]
  SD_card_module1 = SD Card Module

nets:
  VSS: LCM1602_IIC1.VSS, U1.VSS
  VDD: LCM1602_IIC1.VDD, U1.VDD
  N1: LCM1602_IIC1.V0, U1.VO
  N2: LCM1602_IIC1.RS, U1.RS
  N3: LCM1602_IIC1.RW, U1.R_W
  N4: LCM1602_IIC1.E, U1.E
  N5: LCM1602_IIC1.D0, U1.DB0
  N6: LCM1602_IIC1.D1, U1.DB1
  N7: LCM1602_IIC1.D2, U1.DB2
  N8: LCM1602_IIC1.D3, U1.DB3
  N9: LCM1602_IIC1.D4, U1.DB4
  N10: LCM1602_IIC1.D5, U1.DB5
  N11: LCM1602_IIC1.D6, U1.DB6
  N12: LCM1602_IIC1.D7, U1.DB7
  N13: LCM1602_IIC1.A, U1.A
  N14: LCM1602_IIC1.K, U1.K
  N15: LCM1602_IIC1.SDA, M1.D32
  N16: LCM1602_IIC1.SCL, M1.D33, SD_card_module1.GND#7
  N17: LCM1602_IIC1.LED_A, LCM1602_IIC1.LED_B
  N18: M1.GND, SD_card_module1.GND#0
  N19: M1.D34, JP1.2
  N20: M1.D35, JP1.1
  N21: M1.D25, SD_card_module1.MISO
  N22: M1.D26, SD_card_module1.SCK
  N23: M1.D27, SD_card_module1.MOSI
  N24: M1.D14, SD_card_module1.CS
  N25: M1.VIN, SD_card_module1.+5

notes:
  VCC GND RX TX
  PMS 7003

custom parts:
  LCM1602 IIC: I2C-Module to use a 1602 or 2004 LCD on with the wire.h libory Serial LCD Modul
  DOIT Esp32 DevKit v1 (30 pins long, 11 pins width): The DOIT Esp32 DevKit v1 is one of the development board created by DOIT to evaluate the ESP-WROOM-32 module. It is based on the ESP32 microcontroller that boasts Wifi, Bluetooth, Ethernet and Low Power support all in a single chip. (vanepp) made breadboard work, adjusted pin numbering and labels and reduced size of schematic and cleaned up pcb. This chip is 30pins long (2 x15) and 11 pins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
  SD Card Module: SD Card Module Slot Socket Reader For Arduino ARM MCU
